# Fritzing sketch E-vlampios (saved by Fritzing 0.9.3b)

parts:
  Grove1 = Grove 3 Axis Digital Accelerometer 16g
  Part2 = Arduino Mega 2560 (Rev3)
  Raspberry_Pi_3 = Raspberry Pi 3 [part_number=RPI-3-V1.2]
  hc-sr16 = hc-sr04
  hc-sr17 = hc-sr04
  hc-sr18 = hc-sr04
  hc-sr19 = hc-sr04
  hc-sr20 = hc-sr04
  R33 = Resistor [tolerance=±5% resistance=2k package="1206 [SMD]"]
  R34 = Resistor [tolerance=±5% resistance=2k package="1206 [SMD]"]
  R35 = Resistor [tolerance=±5% resistance=2k package="1206 [SMD]"]
  R36 = Resistor [tolerance=±5% resistance=2k package="1206 [SMD]"]
  R37 = Resistor [tolerance=±5% resistance=2k package="1206 [SMD]"]
  R38 = Resistor [tolerance=±5% resistance=1k package="1206 [SMD]"]
  R39 = Resistor [tolerance=±5% resistance=1k package="1206 [SMD]"]
  R40 = Resistor [tolerance=±5% resistance=1k package="1206 [SMD]"]
  R41 = Resistor [tolerance=±5% resistance=1k package="1206 [SMD]"]
  R42 = Resistor [tolerance=±5% resistance=1k package="1206 [SMD]"]
  M1 = DC Motor  # not connected
  M2 = DC Motor  # not connected
  R43 = PHOTOCELL [package=photocell-kit]
  C1 = Capacitor Polarized [package=cpol-radial-100uf-25v]

nets:
  GND: Grove1.GND, Part2.GND
  VCC: Grove1.VCC, Part2.3V3
  N1: Grove1.SDA, Part2.D20/SDA
  N2: Grove1.SCL, Part2.D21/SCL
  N3: Raspberry_Pi_3.GPIO5, Raspberry_Pi_3.GPIO6, Raspberry_Pi_3.GPIO13, Raspberry_Pi_3.GPIO19, Raspberry_Pi_3.GPIO26, Raspberry_Pi_3.GND, R33.Pin_1, R34.Pin_1, R35.Pin_1, R36.Pin_1, R37.Pin_1, R38.Pin_1, R39.Pin_1, R40.Pin_1, R41.Pin_1, R42.Pin_1, C1.-
  N4: Raspberry_Pi_3.GPIO21, hc-sr17.Trig
  N5: Raspberry_Pi_3.GPIO20, hc-sr18.Trig
  N6: Raspberry_Pi_3.GPIO16, hc-sr20.Trig
  N7: Raspberry_Pi_3.GPIO12, hc-sr19.Trig
  N8: Raspberry_Pi_3.ID_SC, hc-sr16.Trig
  N9: Raspberry_Pi_3.GPIO15, R43.P$2
  N10: Raspberry_Pi_3.GPIO14, R43.P$1, C1.+
  VCC_2: Raspberry_Pi_3.5V, hc-sr16.VCC, hc-sr17.VCC, hc-sr18.VCC, hc-sr19.VCC, hc-sr20.VCC
  N11: hc-sr16.Echo, R38.Pin_0
  N12: hc-sr16.GND, R33.Pin_0
  N13: hc-sr17.Echo, R39.Pin_0
  N14: hc-sr17.GND, R34.Pin_0
  N15: hc-sr18.Echo, R40.Pin_0
  N16: hc-sr18.GND, R35.Pin_0
  N17: hc-sr19.Echo, R41.Pin_0
  N18: hc-sr19.GND, R36.Pin_0
  N19: hc-sr20.Echo, R42.Pin_0
  N20: hc-sr20.GND, R37.Pin_0

notes:
  12V
  MD25 motor driver
  HC-SR04 Ultrasonic sensors
  Arduino Mega
  Raspberry Pi 3
  Photocell sensor
  Accelerometer
  Motors
